# Fritzing sketch Clock (saved by Fritzing 0.9.2b)

parts:
  부품1 = Arduino Uno (Rev3)
  부품2 = LED Matrix - Serial Interface - Red/Green/Blue
  부품3 = LED Matrix - Serial Interface - Red/Green/Blue
  IC1 = DS1302 [package="DIP8 [THT]"]
  XTAL1 = CRYSTAL - kHz [frequency="32 kHz"]  # not connected

nets:
  N1: 부품1.D8, IC1.CE_-_Chip_Enable
  N2: 부품1.D10_PWM/SS, 부품2.CS, 부품3.CS
  N3: 부품1.D11_PWM/MOSI, 부품2.SCK, 부품3.SCK
  N4: 부품1.D12/MISO, 부품3.MOSI
  GND: 부품1.GND, 부품2.GND, 부품3.GND, IC1.0V
  N5: 부품1.D6_PWM, IC1.SCLK_-_SPI_Clock
  N6: 부품1.D7, IC1.I/O_-_SPI_Data_In/Out
  VCC: 부품1.5V, 부품2.VCC, 부품3.VCC, IC1.+V
  N7: 부품2.MOSI, 부품3.MISO
